// Logisim project Traffic_Light_Controller_Logisism.circ as structural Verilog: 1 circuit, main circuit main
module main (
);

  wire button_1_out, clock_1_out;
  wire [2:0] counter_1_q, rom_1_data;

  Clock clock_1 (.out(clock_1_out));
  Button button_1 (.out(button_1_out));
  Counter #(.max('h7), .width(3)) counter_1 (
    .clr(button_1_out), .load(button_1_out), .up(clock_1_out), .count(clock_1_out), .clk(clock_1_out),
    .Q(counter_1_q));  // open: D, carry
  ROM #(.addrWidth(3), .dataWidth(3)) rom_1 (.addr(counter_1_q), .data(rom_1_data));
  LED led_1 (.in(rom_1_data[0]));
  LED led_2 (.in(rom_1_data[1]));
  LED led_3 (.in(rom_1_data[2]));

  // Notes on the sheet:
  //   contents of rom_1 (hex, n*v repeats v):
  //   1 3 2 4 0 4 2 1
endmodule
